# Fritzing sketch Schematic (saved by Fritzing 0.9.3b)
breadboards: 1

parts:
  Part1 = Arduino Uno (Rev3)
  LED1 = LED - 5mm [color="Red (633nm)" package="5 mm [THT]"]
  LED2 = LED - 5mm [color="Red (633nm)" package="5 mm [THT]"]
  LED3 = LED - 5mm [color="Red (633nm)" package="5 mm [THT]"]
  LED4 = LED - 5mm [color="Red (633nm)" package="5 mm [THT]"]
  LED5 = LED - 5mm [color="Red (633nm)" package="5 mm [THT]"]
  J1 = Basic Force Sensing Resistor (FSR) [package=THT]
  J2 = Basic Force Sensing Resistor (FSR) [package=THT]
  J3 = Basic Force Sensing Resistor (FSR) [package=THT]
  J4 = Basic Force Sensing Resistor (FSR) [package=THT]
  J5 = Basic Force Sensing Resistor (FSR) [package=THT]
  R1 = Resistor [tolerance=±5% resistance=220 package=THT]
  R2 = Resistor [tolerance=±5% resistance=220 package=THT]
  R3 = Resistor [tolerance=±5% resistance=220 package=THT]
  R4 = Resistor [tolerance=±5% resistance=220 package=THT]
  R5 = Resistor [tolerance=±5% resistance=220 package=THT]
  J6 = Piezo Speaker

nets:
  N1: Part1.A0, J1.pin_0, R5.Pin_1
  N2: Part1.A1, J2.pin_0, R4.Pin_1
  N3: Part1.A2, J3.pin_0, R3.Pin_1
  N4: Part1.A3, J4.pin_0, R2.Pin_1
  N5: Part1.A4/SDA, J5.pin_0, R1.Pin_1
  N6: Part1.D9_PWM, J6.pin2
  N7: Part1.D2, LED1.anode
  N8: Part1.D4, LED3.anode
  N9: Part1.D5_PWM, LED4.anode
  N10: Part1.D7, LED5.anode
  N11: Part1.5V, J1.pin_1, J2.pin_1, J3.pin_1, J4.pin_1, J5.pin_1
  N12: Part1.GND, LED1.cathode, LED2.cathode, LED3.cathode, LED4.cathode, LED5.cathode, R1.Pin_0, R2.Pin_0, R3.Pin_0, R4.Pin_0, R5.Pin_0
